# Fritzing sketch Capstone2 (saved by Fritzing 0.9.3b)
circuit board: 8.63837cm x 6.3636cm
breadboards: 1

parts:
  Raspberry_Pi_1 = Raspberry Pi 3 [part_number=RPI-3-V1.2]
  Part1 = RFID-RC522 [part_number=101218]
  Part2 = Adafruit Ultimate GPS v3 [part_number="Adafruit #746"]
  M2 = STM32F103C8T6 blue mini board
  KEYPAD2 = Membrane Matrix Keypad

nets:
  3V3: Raspberry_Pi_1.3v3, Raspberry_Pi_1.3V3, Part1.3.3V, Part2.VIN, M2.3.3V
  N1: Raspberry_Pi_1.GPIO2, M2.C13
  N2: Raspberry_Pi_1.GPIO3, M2.VBAT
  N3: Raspberry_Pi_1.GPIO4, Part1.RST
  GND: Raspberry_Pi_1.GND, Part1.GND, Part2.GND, M2.G, M2.GND
  N4: Raspberry_Pi_1.GPIO10, Part1.MOSI
  N5: Raspberry_Pi_1.GPIO9, Part1.MISO
  N6: Raspberry_Pi_1.GPIO11, Part1.SCK
  N7: Raspberry_Pi_1.GPIO8, Part1.SDA
  N8: Raspberry_Pi_1.GPIO15, Part2.TX
  N9: Raspberry_Pi_1.GPIO14, Part2.RX
  N10: M2.A12, KEYPAD2.7
  N11: M2.A15, KEYPAD2.6
  N12: M2.B3, KEYPAD2.5
  N13: M2.B4, KEYPAD2.4
  N14: M2.B5, KEYPAD2.3
  N15: M2.B6, KEYPAD2.2
  N16: M2.B7, KEYPAD2.1

notes:
  Ricky Ramnath

custom parts:
  Adafruit Ultimate GPS v3: We carry a few different GPS modules here in the Adafruit shop, but none that satisfied our every desire - that's why we designed this little GPS breakout board. We believe this is the Ultimate GPS module, so we named it that. It's got everything you want and more: -165 dBm sensitivity, 10 Hz updates, 66 channels 5V friendly design and only 20mA current draw Breadboard friendly + two mounting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
  Membrane Matrix Keypad: Membrane Matrix 3x4 Keypad
