# Fritzing sketch CapstoneFinal (saved by Fritzing 0.9.3b)
circuit board: 8.38442cm x 9.00092cm
breadboards: 1

parts:
  Raspberry_Pi_1 = Raspberry Pi 3 [part_number=RPI-3-V1.2]
  Part1 = RFID-RC522 [part_number=101218]
  Part2 = Adafruit Ultimate GPS v3 [part_number="Adafruit #746"]
  KEYPAD2 = Membrane Matrix Keypad

nets:
  3V3: Raspberry_Pi_1.3v3, Raspberry_Pi_1.3V3, Part1.3.3V, Part2.VIN
  N1: Raspberry_Pi_1.GPIO4, KEYPAD2.5
  GND: Raspberry_Pi_1.GND, Part1.GND, Part2.GND
  N2: Raspberry_Pi_1.GPIO17, KEYPAD2.6
  N3: Raspberry_Pi_1.GPIO27, KEYPAD2.1
  N4: Raspberry_Pi_1.GPIO22, KEYPAD2.2
  N5: Raspberry_Pi_1.GPIO10, Part1.MOSI
  N6: Raspberry_Pi_1.GPIO9, Part1.MISO
  N7: Raspberry_Pi_1.GPIO11, Part1.SCK
  N8: Raspberry_Pi_1.GPIO8, Part1.SDA
  N9: Raspberry_Pi_1.GPIO25, Part1.RST
  N10: Raspberry_Pi_1.GPIO24, KEYPAD2.4
  N11: Raspberry_Pi_1.GPIO23, KEYPAD2.3
  N12: Raspberry_Pi_1.GPIO18, KEYPAD2.7
  N13: Raspberry_Pi_1.GPIO15, Part2.TX
  N14: Raspberry_Pi_1.GPIO14, Part2.RX

notes:
  GPS
  RFID
  Keypad
  Ricky
  Mohamed
  Gurkaran

custom parts:
  Adafruit Ultimate GPS v3: We carry a few different GPS modules here in the Adafruit shop, but none that satisfied our every desire - that's why we designed this little GPS breakout board. We believe this is the Ultimate GPS module, so we named it that. It's got everything you want and more: -165 dBm sensitivity, 10 Hz updates, 66 channels 5V friendly design and only 20mA current draw Breadboard friendly + two mounting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
  Membrane Matrix Keypad: Membrane Matrix 3x4 Keypad
