# Fritzing sketch GPS Fritzing2 (saved by Fritzing 0.9.3b)
circuit board: 6.37751cm x 5.09667cm
breadboards: 1

parts:
  Ricky_Ramnath = Raspberry Pi 3 [part_number=RPI-3-V1.2]
  GPS1 = Adafruit Ultimate GPS Breakout
  Part1 = Adafruit Ultimate GPS v3 [part_number="Adafruit #746"]

nets:
  VIN: Ricky_Ramnath.3v3, GPS1.VIN, Part1.VIN
  N1: Ricky_Ramnath.GIPO15, GPS1.TX, Part1.TX
  N2: Ricky_Ramnath.GIPO14, GPS1.RX, Part1.RX
  GND: Ricky_Ramnath.GND, GPS1.GND, Part1.GND
  3.3V: GPS1.3.3V, Part1.3.3V
  N3: GPS1.EN, Part1.ENABLE
  N4: GPS1.VBAT, Part1.VBACKUP
  N5: GPS1.FIX, Part1.FIX
  N6: GPS1.PPS, Part1.1PPS

notes:
  Ricky Ramnath

custom parts:
  Adafruit Ultimate GPS v3: We carry a few different GPS modules here in the Adafruit shop, but none that satisfied our every desire - that's why we designed this little GPS breakout board. We believe this is the Ultimate GPS module, so we named it that. It's got everything you want and more: -165 dBm sensitivity, 10 Hz updates, 66 channels 5V friendly design and only 20mA current draw Breadboard friendly + two mounting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
