# Fritzing sketch GPS Fritzing3 (saved by Fritzing 0.9.3b)
circuit board: 3.06756cm x 5.58446cm
breadboards: 1

parts:
  GPS1 = Adafruit Ultimate GPS Breakout
  Part1 = Adafruit Ultimate GPS v3 [part_number="Adafruit #746"]
  Raspberry_Pi_1 = Raspberry Pi 3 [part_number=RPI-3-V1.2]  # not connected
  J1 = double row rounded female pin header, 10 pins [form="♀ (female rounded)"]

nets:
  3.3V: GPS1.3.3V, Part1.3.3V
  N1: GPS1.EN, Part1.ENABLE
  N2: GPS1.VBAT, Part1.VBACKUP
  N3: GPS1.FIX, Part1.FIX
  N4: GPS1.TX, Part1.TX, J1.pin1
  N5: GPS1.RX, Part1.RX, J1.pin2
  GND: GPS1.GND, Part1.GND, J1.pin3
  VIN: GPS1.VIN, Part1.VIN, J1.pin6
  N6: GPS1.PPS, Part1.1PPS

notes:
  Ricky Ramnath
  GND
  TX
  RX
  3.3V

custom parts:
  Adafruit Ultimate GPS v3: We carry a few different GPS modules here in the Adafruit shop, but none that satisfied our every desire - that's why we designed this little GPS breakout board. We believe this is the Ultimate GPS module, so we named it that. It's got everything you want and more: -165 dBm sensitivity, 10 Hz updates, 66 channels 5V friendly design and only 20mA current draw Breadboard friendly + two mounting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
